// Digital circuit Test Sandbox.dig as structural Verilog
module Test_Sandbox (
  input  clk
);

  wire button_1_out, button_2_out, glass_cpu_1_p12, glass_cpu_1_p14, glass_cpu_1_p15, glass_cpu_1_p16;
  wire [15:0] add_1_s, glass_cpu_1_p4, glass_cpu_1_p10, glass_cpu_1_p11, glass_cpu_1_p13;
  wire [31:0] counter_1_out;

  Button button_1 (.out(button_1_out));
  Button button_2 (.out(button_2_out));
  // Glass_CPU glass_cpu_1: pin names not known; wires that end beside it: button_1_out, button_2_out, clk, glass_cpu_1_p4, 1'b1, 1'b1, 4'b0000, 4'b0000, 1'b0, glass_cpu_1_p10, glass_cpu_1_p11, glass_cpu_1_p12, glass_cpu_1_p13, glass_cpu_1_p14, glass_cpu_1_p15, glass_cpu_1_p16
  LED led_1 (.in(glass_cpu_1_p16));
  Counter #(.Bits(32)) counter_1 (.en(1'b1), .C(glass_cpu_1_p15), .clr(1'b0), .out(counter_1_out));  // open: ovf
  Add #(.Bits(16)) add_1 (.a(glass_cpu_1_p13), .b(16'h2), .c_i(1'b0), .s(add_1_s));  // open: c_o
  RAMDualPort #(.AddrBits(16), .isProgramMemory("true"), .Bits(16)) Program_Memory (
    .A(glass_cpu_1_p10), .Din(glass_cpu_1_p11), .str(glass_cpu_1_p12), .C(clk), .ld(1'b1), .D(glass_cpu_1_p4));
  // Probe Memory Address on glass_cpu_1_p10
  // Probe Cycles Used on counter_1_out
  // Probe RTL Line on add_1_s
  // Probe Test IOP on glass_cpu_1_p14

  // Notes on the sheet:
  //   clk: Hz: 32
endmodule
